// Logisim project 1-bit_adder.circ as structural Verilog
module _2_bitArithmetic (
  input  Cin,
  input  S0,
  input  S1,
  input  [1:0] A_i,
  input  [1:0] B_i,
  output D_i,
  output C_i_2
);

  wire n1_bit_arithmetic_1_c_i_1;

  _1_bit_Arithmetic u_1_bit_arithmetic_1 (
    .Cin(Cin), .S0(S0), .S1(S1), .A_i(A_i[0]), .B_i(B_i[0]), .D_i(D_i), .C_i_1(n1_bit_arithmetic_1_c_i_1));
  _1_bit_Arithmetic u_1_bit_arithmetic_2 (
    .Cin(n1_bit_arithmetic_1_c_i_1), .S0(S0), .S1(S1), .A_i(A_i[1]), .B_i(B_i[1]), .C_i_1(C_i_2));  // open: D_i
endmodule

module _1_bit_Logic (
  input  [1:0] S1_S0,
  input  A_i,
  input  B_i,
  output F_i
);

  wire and_1_out, not_1_out, or_1_out, xor_1_out;

  and and_1 (and_1_out, A_i, B_i);
  or or_1 (or_1_out, A_i, B_i);
  xor xor_1 (xor_1_out, A_i, B_i);
  not not_1 (not_1_out, A_i);
  Multiplexer #(.select(2)) multiplexer_1 (
    .in0(and_1_out), .in1(or_1_out), .in2(xor_1_out), .in3(not_1_out), .out(F_i), .sel(S1_S0));  // open: en
endmodule

module _2_bit_Logic (
  input  [1:0] S1_S0,
  input  [1:0] A,
  input  [1:0] B,
  output F_i,
  output F_i_1
);

  _1_bit_Logic u_1_bit_logic_1 (.S1_S0(S1_S0), .A_i(A[0]), .B_i(B[0]), .F_i(F_i));
  _1_bit_Logic u_1_bit_logic_2 (.S1_S0(S1_S0), .A_i(A[1]), .B_i(B[1]), .F_i(F_i_1));
endmodule

module _1_bit_Arithmetic (
  input  Cin,
  input  S0,
  input  S1,
  input  A_i,
  input  B_i,
  output D_i,
  output C_i_1
);

  wire multiplexer_1_out, not_1_out, not_2_out;

  not not_1 (not_1_out, B_i);
  not not_2 (not_2_out, 1'b0);
  Multiplexer #(.select(2)) multiplexer_1 (
    .in0(B_i), .in1(not_1_out), .in2(1'b0), .in3(not_2_out), .out(multiplexer_1_out), .sel({S1, S0}));  // open: en
  Adder #(.width(1)) adder_1 (.a(A_i), .b(multiplexer_1_out), .out(D_i), .cin(Cin), .cout(C_i_1));
endmodule
