// Logisim project 8-bit_register.circ as structural Verilog: 1 circuit, main circuit main
module main (
  input  [7:0] Bus_Input,
  input  increment,
  input  Load,
  input  CLR,
  output [7:0] Z,
  output C_out
);

  wire or_1_out;
  wire [7:0] adder_1_out, multiplexer_1_out;

  Adder adder_1 (.a(Z), .b({8{1'b1}}), .out(adder_1_out), .cout(C_out));  // open: cin
  Multiplexer #(.width(8)) multiplexer_1 (
    .in0(Bus_Input), .in1(adder_1_out), .out(multiplexer_1_out), .sel(increment));  // open: en
  or or_1 (or_1_out, increment, Load);
  Register register_1 (.D(multiplexer_1_out), .Q(Z), .clk(or_1_out), .clr(CLR));  // open: en
endmodule
